// Logisim project EL.circ as structural Verilog
module main (
  input  in_1,
  input  in_2,
  input  in_3,
  input  in_4,
  input  in_5,
  input  in_6,
  input  in_7,
  input  in_8,
  input  subtraction,
  input  in_10,
  input  in_11,
  input  in_12,
  input  in_13,
  input  in_14,
  input  in_15,
  input  in_16,
  input  in_17,
  input  in_18,
  input  in_19,
  input  in_20,
  input  in_21,
  input  in_22,
  input  in_23,
  input  in_24,
  input  initial_charges,
  input  in_26,
  input  in_27,
  input  in_28,
  input  in_29,
  input  in_30,
  input  in_31,
  input  in_32,
  input  in_33
);

  wire and_1_out, and_3_out, and_4_out, and_5_out, and_6_out, and_7_out, and_8_out, and_9_out, ic_74283_1_p2,
       ic_74283_1_p3, ic_74283_1_p5, ic_74283_1_p6, ic_74283_1_p7, ic_74283_1_p8, ic_74283_1_p9,
       ic_74283_2_p2, ic_74283_2_p3, ic_74283_2_p9, ic_74283_2_p11, ic_74283_2_p13, ic_74283_2_p14,
       ic_74283_2_p15, ic_74283_3_p1, ic_74283_3_p3, ic_74283_3_p8, ic_74283_3_p10, ic_74283_3_p11,
       ic_74283_3_p12, ic_74283_3_p13, ic_74283_3_p14, ic_74283_3_p15, ic_74283_4_p2, ic_74283_4_p7,
       ic_74283_4_p8, ic_74283_4_p9, ic_74283_4_p10, ic_74283_4_p11, ic_74283_4_p12, ic_74283_4_p14,
       ic_74283_5_p2, ic_74283_5_p8, ic_74283_5_p9, ic_74283_5_p10, ic_74283_5_p11, ic_74283_5_p12,
       ic_74283_5_p13, ic_74283_5_p14, ic_74283_6_p2, ic_74283_6_p7, ic_74283_6_p9, ic_74283_6_p10,
       ic_74283_6_p11, ic_74283_6_p12, ic_74283_6_p13, ic_74283_6_p14, ic_74283_7_p1, ic_74283_7_p4,
       ic_74283_7_p6, ic_74283_7_p8, ic_74283_7_p10, ic_74283_8_p8, ic_74283_8_p10, ic_74283_8_p11,
       ic_74283_8_p12, ic_74283_8_p13, ic_74283_8_p14, ic_74283_9_p4, ic_74283_9_p6, ic_74283_9_p8,
       ic_74283_9_p9, ic_74283_9_p10, multiplexer_1_out, multiplexer_2_out, multiplexer_3_out,
       multiplexer_4_out, multiplexer_5_out, multiplexer_6_out, multiplexer_7_out, multiplexer_8_out,
       multiplexer_9_out, multiplexer_10_out, multiplexer_11_out, multiplexer_12_out, xor_1_out, xor_2_out,
       xor_3_out, xor_5_out, xor_6_out;

  Multiplexer multiplexer_1 (
    .in0(in_24), .in1(ic_74283_1_p3), .out(multiplexer_1_out), .sel(ic_74283_2_p3));  // open: en
  // IC_74283 ic_74283_1: pin names not known; wires that end beside it: in_20, ic_74283_1_p2, ic_74283_1_p3, in_24, ic_74283_1_p5, ic_74283_1_p6, ic_74283_1_p7, ic_74283_1_p8, ic_74283_1_p9
  Multiplexer multiplexer_2 (
    .in0(in_24), .in1(ic_74283_1_p5), .out(multiplexer_2_out), .sel(ic_74283_2_p3));  // open: en
  and and_1 (and_1_out, in_19, ic_74283_2_p9);
  and and_2 (ic_74283_1_p6, in_18, ic_74283_2_p9, ic_74283_6_p2);
  Multiplexer multiplexer_3 (
    .in0(in_24), .in1(ic_74283_1_p7), .out(multiplexer_3_out), .sel(ic_74283_2_p3));  // open: en
  xor xor_1 (xor_1_out, subtraction, in_6);
  xor xor_2 (xor_2_out, subtraction, in_5);
  and and_3 (and_3_out, in_19, ic_74283_8_p10);
  and and_4 (and_4_out, in_19, ic_74283_8_p8);
  and and_5 (and_5_out, in_19, ic_74283_2_p11);
  xor xor_3 (xor_3_out, subtraction, in_7);
  // IC_74283 ic_74283_2: pin names not known; wires that end beside it: subtraction, ic_74283_2_p2, ic_74283_2_p3, in_15, in_16, in_17, in_11, xor_2_out, ic_74283_2_p9, xor_1_out, ic_74283_2_p11, xor_3_out, ic_74283_2_p13, ic_74283_2_p14, ic_74283_2_p15
  and and_6 (and_6_out, in_19, ic_74283_8_p12);
  and and_7 (and_7_out, in_19, ic_74283_2_p13);
  Multiplexer multiplexer_4 (
    .in0(in_24), .in1(ic_74283_1_p9), .out(multiplexer_4_out), .sel(ic_74283_2_p3));  // open: en
  and and_8 (and_8_out, in_19, ic_74283_8_p14);
  // IC_74283 ic_74283_3: pin names not known; wires that end beside it: ic_74283_3_p1, in_21, ic_74283_3_p3, and_4_out, and_3_out, and_6_out, and_8_out, ic_74283_3_p8, ic_74283_3_p1, ic_74283_3_p10, ic_74283_3_p11, ic_74283_3_p12, ic_74283_3_p13, ic_74283_3_p14, ic_74283_3_p15, in_19
  // IC_74283 ic_74283_4: pin names not known; wires that end beside it: ic_74283_3_p3, ic_74283_4_p2, ic_74283_3_p1, ic_74283_3_p11, ic_74283_3_p13, ic_74283_3_p15, ic_74283_4_p7, ic_74283_4_p8, ic_74283_4_p9, ic_74283_4_p10, ic_74283_4_p11, ic_74283_4_p12, in_22, ic_74283_4_p14, in_19
  and and_9 (and_9_out, in_19, ic_74283_2_p15);
  // IC_74283 ic_74283_5: pin names not known; wires that end beside it: ic_74283_4_p2, ic_74283_5_p2, and_1_out, and_5_out, and_7_out, and_9_out, in_23, ic_74283_5_p8, ic_74283_5_p9, ic_74283_5_p10, ic_74283_5_p11, ic_74283_5_p12, ic_74283_5_p13, ic_74283_5_p14
  // IC_74283 ic_74283_6: pin names not known; wires that end beside it: ic_74283_5_p2, ic_74283_6_p2, ic_74283_5_p8, ic_74283_5_p10, ic_74283_5_p12, ic_74283_5_p14, ic_74283_6_p7, ic_74283_1_p8, ic_74283_6_p9, ic_74283_6_p10, ic_74283_6_p11, ic_74283_6_p12, ic_74283_6_p13, ic_74283_6_p14
  Multiplexer multiplexer_5 (
    .in0(in_29), .in1(ic_74283_7_p4), .out(multiplexer_5_out), .sel(ic_74283_2_p3));  // open: en
  xor xor_4 (ic_74283_2_p14, subtraction, in_8);
  and and_10 (ic_74283_3_p8, in_20, ic_74283_2_p15);
  and and_11 (ic_74283_4_p7, in_18, ic_74283_8_p10);
  and and_12 (ic_74283_6_p7, in_18, ic_74283_2_p11);
  // IC_74283 ic_74283_7: pin names not known; wires that end beside it: ic_74283_7_p1, ic_74283_1_p2, ic_74283_6_p10, ic_74283_7_p4, ic_74283_6_p12, ic_74283_7_p6, ic_74283_6_p14, ic_74283_7_p8, ic_74283_4_p8, ic_74283_7_p10
  Multiplexer multiplexer_6 (
    .in0(in_30), .in1(ic_74283_7_p6), .out(multiplexer_6_out), .sel(ic_74283_2_p3));  // open: en
  and and_13 (ic_74283_3_p10, in_20, ic_74283_8_p8);
  and and_14 (ic_74283_4_p9, in_18, ic_74283_8_p12);
  and and_15 (ic_74283_5_p9, in_20, ic_74283_2_p9);
  and and_16 (ic_74283_6_p9, in_18, ic_74283_2_p13);
  Multiplexer multiplexer_7 (
    .in0(in_31), .in1(ic_74283_7_p8), .out(multiplexer_7_out), .sel(ic_74283_2_p3));  // open: en
  xor xor_5 (xor_5_out, subtraction, in_1);
  and and_17 (ic_74283_3_p12, in_20, ic_74283_8_p10);
  and and_18 (ic_74283_4_p11, in_18, ic_74283_8_p14);
  and and_19 (ic_74283_5_p11, in_20, ic_74283_2_p11);
  and and_20 (ic_74283_5_p13, in_20, ic_74283_2_p13);
  and and_21 (ic_74283_6_p11, in_18, ic_74283_2_p15);
  and and_22 (ic_74283_6_p13, in_18, ic_74283_8_p8);
  xor xor_6 (xor_6_out, subtraction, in_2);
  // IC_74283 ic_74283_8: pin names not known; wires that end beside it: subtraction, ic_74283_2_p2, in_12, in_13, in_14, in_10, xor_5_out, ic_74283_8_p8, xor_6_out, ic_74283_8_p10, ic_74283_8_p11, ic_74283_8_p12, ic_74283_8_p13, ic_74283_8_p14
  and and_23 (ic_74283_3_p14, in_20, ic_74283_8_p12);
  Multiplexer multiplexer_8 (
    .in0(in_32), .in1(ic_74283_7_p10), .out(multiplexer_8_out), .sel(ic_74283_2_p3));  // open: en
  xor xor_7 (ic_74283_8_p11, subtraction, in_3);
  Multiplexer multiplexer_9 (
    .in0(initial_charges), .in1(ic_74283_9_p4), .out(multiplexer_9_out), .sel(ic_74283_2_p3));  // open: en
  xor xor_8 (ic_74283_8_p13, subtraction, in_4);
  // IC_74283 ic_74283_9: pin names not known; wires that end beside it: in_33, ic_74283_7_p1, ic_74283_4_p10, ic_74283_9_p4, ic_74283_4_p12, ic_74283_9_p6, ic_74283_4_p14, ic_74283_9_p8, ic_74283_9_p9, ic_74283_9_p10
  Multiplexer multiplexer_10 (
    .in0(in_26), .in1(ic_74283_9_p6), .out(multiplexer_10_out), .sel(ic_74283_2_p3));  // open: en
  and and_24 (ic_74283_9_p9, in_20, ic_74283_8_p14);
  Multiplexer multiplexer_11 (
    .in0(in_27), .in1(ic_74283_9_p8), .out(multiplexer_11_out), .sel(ic_74283_2_p3));  // open: en
  Multiplexer multiplexer_12 (
    .in0(in_28), .in1(ic_74283_9_p10), .out(multiplexer_12_out), .sel(ic_74283_2_p3));  // open: en

  // Notes on the sheet:
  //   per km fare
  //   mandatory distance
  //   distance of travel
endmodule

module bcd_converter (
  input  in_1,
  input  in_2,
  input  in_3,
  input  in_4,
  input  in_5,
  input  in_6,
  input  in_7,
  input  in_8,
  input  in_9,
  input  in_10,
  input  in_11,
  input  in_12,
  input  feed,
  output q0,
  output q1,
  output q2,
  output q3,
  output q4,
  output q5,
  output q6,
  output q7,
  output q8,
  output q9
);

  wire and_1_out, and_2_out, and_3_out, and_4_out, and_5_out, and_6_out, and_7_out, and_8_out, and_9_out,
       and_10_out, and_11_out, and_12_out, and_13_out, and_14_out, and_15_out, and_16_out, and_17_out,
       and_18_out, and_19_out, and_20_out, and_21_out, and_22_out, and_23_out, and_24_out, and_25_out,
       and_26_out, and_27_out, and_28_out, and_29_out, and_30_out, and_31_out, and_32_out, and_33_out,
       and_34_out, and_35_out, and_36_out, and_37_out, and_38_out, and_39_out, and_40_out, and_41_out,
       and_42_out, clock_1_out, clock_2_out, d_flip_flop_1_p3, d_flip_flop_2_p3, d_flip_flop_3_p3,
       d_flip_flop_3_p4, d_flip_flop_3_p5, d_flip_flop_4_p3, ic_7485_1_p1, ic_7485_1_p2, ic_7485_1_p4,
       ic_7485_1_p5, ic_7485_1_p6, ic_7485_1_p7, ic_7485_1_p16, ic_7485_2_p8, ic_74283_1_p1, ic_74283_1_p2,
       ic_74283_1_p3, ic_74283_1_p4, ic_74283_1_p5, ic_74283_1_p6, ic_74283_1_p7, ic_74283_1_p16,
       ic_74283_2_p8, ic_74283_2_p10, ic_74283_2_p11, ic_74283_2_p12, ic_74283_2_p13, ic_74283_2_p14,
       multiplexer_1_out, multiplexer_2_out, multiplexer_3_out, multiplexer_4_out, multiplexer_5_out,
       multiplexer_6_out, multiplexer_7_out, multiplexer_8_out, multiplexer_9_out, not_1_out, not_2_out,
       or_1_out, or_2_out, or_3_out, or_4_out, or_5_out, or_6_out, or_7_out, or_8_out, or_9_out, or_10_out,
       or_11_out, or_12_out, or_13_out, or_14_out, or_15_out, or_16_out, or_17_out, or_18_out, or_19_out,
       or_20_out, or_21_out, or_22_out, quotient_clk_out, xor_1_out, xor_2_out;

  not not_1 (not_1_out, feed);
  Clock clock_1 (.out(clock_1_out));
  and and_1 (and_1_out, d_flip_flop_1_p3, feed);
  or or_1 (or_1_out, and_1_out, and_2_out);
  // D_Flip_Flop d_flip_flop_1: pin names not known; wires that end beside it: in_9, clock_1_out, d_flip_flop_1_p3
  or or_2 (or_2_out, ic_7485_1_p5, ic_7485_1_p7);
  // IC_74283 ic_74283_1: pin names not known; wires that end beside it: ic_74283_1_p1, ic_74283_1_p2, ic_74283_1_p3, ic_74283_1_p4, ic_74283_1_p5, ic_74283_1_p6, ic_74283_1_p7, 1'b0, 1'b0, 1'b0, ic_74283_1_p1, 1'b1, 1'b1, 1'b1, 1'b1, ic_74283_1_p16, ic_74283_1_p1
  and and_2 (and_2_out, not_1_out, in_5);
  and and_3 (and_3_out, d_flip_flop_2_p3, feed);
  // D_Flip_Flop d_flip_flop_2: pin names not known; wires that end beside it: or_1_out, clock_1_out, d_flip_flop_2_p3
  // IC_7485 ic_7485_1: pin names not known; wires that end beside it: ic_7485_1_p1, ic_7485_1_p2, ic_7485_1_p1, ic_7485_1_p4, ic_7485_1_p5, ic_7485_1_p6, ic_7485_1_p7, 1'b0, 1'b0, 1'b0, ic_74283_1_p1, 1'b0, 1'b0, 1'b0, 1'b0, ic_7485_1_p16
  and and_4 (and_4_out, not_1_out, in_6);
  or or_3 (or_3_out, and_3_out, and_4_out);
  and and_5 (and_5_out, d_flip_flop_3_p4, feed);
  or or_4 (or_4_out, and_5_out, and_6_out);
  // D_Flip_Flop d_flip_flop_3: pin names not known; wires that end beside it: or_3_out, clock_1_out, d_flip_flop_3_p3, d_flip_flop_3_p4, d_flip_flop_3_p5
  and and_6 (and_6_out, not_1_out, in_10);
  // D_Flip_Flop d_flip_flop_4: pin names not known; wires that end beside it: or_4_out, clock_1_out, d_flip_flop_4_p3
  // IC_7485 ic_7485_2: pin names not known; wires that end beside it: 1'b0, ic_7485_1_p2, 1'b1, ic_7485_1_p4, 1'b0, ic_7485_1_p6, ic_74283_1_p2, ic_7485_2_p8, ic_74283_1_p3, ic_74283_1_p4, ic_74283_1_p5, 1'b1, 1'b0, d_flip_flop_4_p3, 1'b1, 1'b0, d_flip_flop_3_p4
  Multiplexer multiplexer_1 (.in0(1'b0), .in1(1'b1), .out(multiplexer_1_out), .sel(or_2_out));  // open: en
  Multiplexer multiplexer_2 (.in0(1'b0), .in1(1'b0), .out(multiplexer_2_out), .sel(or_2_out));  // open: en
  xor xor_1 (xor_1_out, or_2_out, multiplexer_2_out);
  xor xor_2 (xor_2_out, or_2_out, multiplexer_1_out);
  // IC_74283 ic_74283_2: pin names not known; wires that end beside it: or_2_out, ic_74283_1_p6, ic_74283_1_p2, ic_74283_1_p3, ic_74283_1_p4, ic_74283_1_p5, xor_2_out, ic_74283_2_p8, xor_1_out, ic_74283_2_p10, ic_74283_2_p11, ic_74283_2_p12, ic_74283_2_p13, ic_74283_2_p14
  and and_7 (and_7_out, d_flip_flop_4_p3, feed);
  or or_5 (or_5_out, and_7_out, and_8_out);
  Multiplexer multiplexer_3 (.in0(1'b0), .in1(1'b1), .out(multiplexer_3_out), .sel(or_2_out));  // open: en
  xor xor_3 (ic_74283_2_p11, or_2_out, multiplexer_3_out);
  and and_8 (and_8_out, not_1_out, in_7);
  // D_Flip_Flop d_flip_flop_5: pin names not known; wires that end beside it: d_flip_flop_2_p3, or_5_out, clock_1_out, ic_7485_2_p8, d_flip_flop_1_p3
  Multiplexer multiplexer_4 (.in0(1'b0), .in1(1'b0), .out(multiplexer_4_out), .sel(or_2_out));  // open: en
  xor xor_4 (ic_74283_2_p13, or_2_out, multiplexer_4_out);
  and and_9 (and_9_out, not_1_out, in_8);
  and and_10 (and_10_out, ic_7485_2_p8, feed);
  or or_6 (or_6_out, and_10_out, and_9_out);
  and and_11 (and_11_out, d_flip_flop_3_p5, feed);
  or or_7 (or_7_out, and_11_out, and_12_out);
  // D_Flip_Flop d_flip_flop_6: pin names not known; wires that end beside it: or_6_out, clock_1_out, d_flip_flop_3_p5
  not not_2 (not_2_out, 1'b1);
  Clock quotient_clk (.out(quotient_clk_out));
  and and_12 (and_12_out, not_1_out, in_11);
  // D_Flip_Flop d_flip_flop_7: pin names not known; wires that end beside it: or_7_out, clock_1_out, d_flip_flop_3_p3, d_flip_flop_3_p3
  and and_13 (and_13_out, not_2_out, 1'b0);
  and and_14 (and_14_out, q0, 1'b1);
  or or_8 (or_8_out, and_14_out, and_13_out);
  // D_Flip_Flop d_flip_flop_8: pin names not known; wires that end beside it: or_2_out, quotient_clk_out, q0
  and and_15 (and_15_out, q1, 1'b1);
  // D_Flip_Flop d_flip_flop_9: pin names not known; wires that end beside it: or_8_out, quotient_clk_out, q1
  and and_16 (and_16_out, d_flip_flop_3_p3, feed);
  and and_17 (and_17_out, not_1_out, in_12);
  or or_9 (or_9_out, and_16_out, and_17_out);
  and and_18 (and_18_out, not_2_out, 1'b0);
  or or_10 (or_10_out, and_15_out, and_18_out);
  // D_Flip_Flop d_flip_flop_10: pin names not known; wires that end beside it: or_10_out, quotient_clk_out, q2
  and and_19 (and_19_out, ic_7485_1_p16, feed);
  or or_11 (or_11_out, and_19_out, and_22_out);
  // D_Flip_Flop d_flip_flop_11: pin names not known; wires that end beside it: or_9_out, clock_1_out, ic_7485_1_p16
  Clock clock_2 (.out(clock_2_out));
  and and_20 (and_20_out, q2, 1'b1);
  and and_21 (and_21_out, not_2_out, 1'b0);
  or or_12 (or_12_out, and_20_out, and_21_out);
  Multiplexer multiplexer_5 (
    .in0(in_1), .in1(ic_74283_2_p14), .out(multiplexer_5_out), .sel(ic_74283_1_p7));  // open: en
  and and_22 (and_22_out, not_1_out, multiplexer_5_out);
  // D_Flip_Flop d_flip_flop_12: pin names not known; wires that end beside it: or_11_out, clock_2_out, ic_74283_1_p5
  // D_Flip_Flop d_flip_flop_13: pin names not known; wires that end beside it: or_12_out, quotient_clk_out, q3
  Multiplexer multiplexer_6 (
    .in0(in_2), .in1(ic_74283_2_p12), .out(multiplexer_6_out), .sel(ic_74283_1_p7));  // open: en
  and and_23 (and_23_out, not_1_out, multiplexer_6_out);
  and and_24 (and_24_out, ic_74283_1_p5, feed);
  or or_13 (or_13_out, and_24_out, and_23_out);
  and and_25 (and_25_out, q3, 1'b1);
  or or_14 (or_14_out, and_25_out, and_26_out);
  // D_Flip_Flop d_flip_flop_14: pin names not known; wires that end beside it: or_13_out, clock_2_out, ic_74283_1_p4
  and and_26 (and_26_out, not_2_out, 1'b0);
  and and_27 (and_27_out, q4, 1'b1);
  // D_Flip_Flop d_flip_flop_15: pin names not known; wires that end beside it: or_14_out, quotient_clk_out, q4
  and and_28 (and_28_out, ic_74283_1_p4, feed);
  or or_15 (or_15_out, and_28_out, and_30_out);
  and and_29 (and_29_out, not_2_out, 1'b0);
  or or_16 (or_16_out, and_27_out, and_29_out);
  Multiplexer multiplexer_7 (
    .in0(in_3), .in1(ic_74283_2_p10), .out(multiplexer_7_out), .sel(ic_74283_1_p7));  // open: en
  and and_30 (and_30_out, not_1_out, multiplexer_7_out);
  // D_Flip_Flop d_flip_flop_16: pin names not known; wires that end beside it: or_15_out, clock_2_out, ic_74283_1_p3
  and and_31 (and_31_out, q5, 1'b1);
  or or_17 (or_17_out, and_31_out, and_34_out);
  // D_Flip_Flop d_flip_flop_17: pin names not known; wires that end beside it: or_16_out, quotient_clk_out, q5
  Multiplexer multiplexer_8 (
    .in0(in_4), .in1(ic_74283_2_p8), .out(multiplexer_8_out), .sel(ic_74283_1_p7));  // open: en
  and and_32 (and_32_out, ic_74283_1_p3, feed);
  and and_33 (and_33_out, not_1_out, multiplexer_8_out);
  or or_18 (or_18_out, and_32_out, and_33_out);
  and and_34 (and_34_out, not_2_out, 1'b0);
  // D_Flip_Flop d_flip_flop_18: pin names not known; wires that end beside it: or_17_out, quotient_clk_out
  and and_35 (and_35_out, ic_74283_1_p2, feed);
  or or_19 (or_19_out, and_35_out, and_37_out);
  // D_Flip_Flop d_flip_flop_19: pin names not known; wires that end beside it: or_18_out, clock_2_out, ic_74283_1_p2
  and and_36 (and_36_out, q6, 1'b1);
  or or_20 (or_20_out, and_36_out, and_38_out);
  Multiplexer multiplexer_9 (
    .in0(1'b0), .in1(ic_74283_1_p16), .out(multiplexer_9_out), .sel(ic_74283_1_p7));  // open: en
  and and_37 (and_37_out, not_1_out, multiplexer_9_out);
  // D_Flip_Flop d_flip_flop_20: pin names not known; wires that end beside it: or_19_out, clock_2_out, ic_74283_1_p1, ic_74283_1_p7, not_1_out, feed
  and and_38 (and_38_out, not_2_out, 1'b0);
  and and_39 (and_39_out, q7, 1'b1);
  // D_Flip_Flop d_flip_flop_21: pin names not known; wires that end beside it: or_20_out, quotient_clk_out, q7
  and and_40 (and_40_out, not_2_out, 1'b0);
  or or_21 (or_21_out, and_39_out, and_40_out);
  and and_41 (and_41_out, q8, 1'b1);
  or or_22 (or_22_out, and_41_out, and_42_out);
  // D_Flip_Flop d_flip_flop_22: pin names not known; wires that end beside it: or_21_out, quotient_clk_out, q8, q8
  and and_42 (and_42_out, not_2_out, 1'b0);
  // D_Flip_Flop d_flip_flop_23: pin names not known; wires that end beside it: or_22_out, quotient_clk_out, q9, q9

  // Notes on the sheet:
  //   13  bit shift register
  //   1 for all
  //   feed and shift
  //   1
  //   1
  //   0-initial
  //   LSB
  //   MSB
endmodule

module BCD_7segment (
  input  D,
  input  C,
  input  B,
  input  A,
  output a_2,
  output b_2,
  output c_2,
  output d_2,
  output e,
  output f,
  output g
);

  wire and_1_out, and_2_out, and_3_out, and_4_out, and_5_out, and_6_out, and_7_out, and_8_out, and_9_out,
       and_10_out, and_11_out, and_12_out, and_13_out, and_14_out, and_15_out, and_16_out, and_17_out,
       not_1_out, not_2_out, not_3_out, not_4_out, not_5_out, not_6_out, not_7_out, not_8_out, not_9_out,
       not_10_out, not_11_out, not_12_out, not_13_out, not_14_out, not_15_out, not_16_out, not_17_out,
       not_18_out, not_19_out, not_20_out, not_21_out, or_1_out, or_2_out, or_4_out, or_5_out, or_8_out,
       or_9_out, or_10_out, or_12_out, or_14_out, or_15_out, or_17_out;

  not not_1 (not_1_out, C);
  not not_2 (not_2_out, A);
  not not_3 (not_3_out, B);
  not not_4 (not_4_out, A);
  not not_5 (not_5_out, B);
  not not_6 (not_6_out, C);
  not not_7 (not_7_out, A);
  not not_8 (not_8_out, C);
  not not_9 (not_9_out, B);
  not not_10 (not_10_out, C);
  not not_11 (not_11_out, A);
  not not_12 (not_12_out, A);
  not not_13 (not_13_out, B);
  not not_14 (not_14_out, A);
  not not_15 (not_15_out, B);
  not not_16 (not_16_out, A);
  not not_17 (not_17_out, C);
  not not_18 (not_18_out, B);
  not not_19 (not_19_out, A);
  and and_1 (and_1_out, not_1_out, not_2_out);
  and and_2 (and_2_out, C, A);
  not not_20 (not_20_out, C);
  and and_3 (and_3_out, not_3_out, not_4_out);
  or or_1 (or_1_out, not_5_out, A);
  and and_4 (and_4_out, not_6_out, not_7_out);
  and and_5 (and_5_out, not_8_out, B);
  not not_21 (not_21_out, A);
  and and_6 (and_6_out, C, not_9_out);
  and and_7 (and_7_out, not_10_out, not_11_out);
  and and_8 (and_8_out, B, not_12_out);
  and and_9 (and_9_out, not_13_out, not_14_out);
  and and_10 (and_10_out, C, not_15_out);
  and and_11 (and_11_out, C, not_16_out);
  and and_12 (and_12_out, not_17_out, B);
  and and_13 (and_13_out, C, not_18_out);
  and and_14 (and_14_out, C, not_19_out);
  or or_2 (or_2_out, and_1_out, B);
  or or_3 (a_2, or_2_out, or_4_out);
  or or_4 (or_4_out, and_2_out, D);
  or or_5 (or_5_out, not_20_out, and_3_out);
  or or_6 (b_2, or_5_out, and_15_out);
  and and_15 (and_15_out, B, A);
  or or_7 (c_2, or_1_out, C);
  or or_8 (or_8_out, and_4_out, and_5_out);
  or or_9 (or_9_out, or_8_out, and_16_out);
  and and_16 (and_16_out, B, not_21_out);
  and and_17 (and_17_out, and_6_out, A);
  or or_10 (or_10_out, and_17_out, D);
  or or_11 (e, and_7_out, and_8_out);
  or or_12 (or_12_out, and_9_out, and_10_out);
  or or_13 (f, or_12_out, or_14_out);
  or or_14 (or_14_out, and_11_out, D);
  or or_15 (or_15_out, and_12_out, and_13_out);
  or or_16 (g, or_15_out, or_17_out);
  or or_17 (or_17_out, and_14_out, D);
  or or_18 (d_2, or_9_out, or_10_out);
endmodule

module quotient_register (
  input  serial_input,
  output q0,
  output q1,
  output q2,
  output q3,
  output q4,
  output q5,
  output q6,
  output q7,
  output q8,
  output q9
);

  wire and_1_out, and_2_out, and_3_out, and_4_out, and_5_out, and_6_out, and_7_out, and_8_out, and_9_out,
       and_10_out, and_11_out, and_12_out, and_13_out, and_14_out, and_15_out, and_16_out, and_17_out,
       and_18_out, not_1_out, or_1_out, or_2_out, or_3_out, or_4_out, or_5_out, or_6_out, or_7_out, or_8_out,
       or_9_out, quotient_clk_out;

  not not_1 (not_1_out, 1'b1);
  and and_1 (and_1_out, q0, 1'b1);
  D_Flip_Flop d_ff_1 (
    .clk(quotient_clk_out), .D(serial_input), .Q(q0), .preset(1'b0), .en(1'b1), .reset(1'b0));  // open: Qn
  Clock quotient_clk (.out(quotient_clk_out));
  and and_2 (and_2_out, not_1_out, 1'b0);
  or or_1 (or_1_out, and_1_out, and_2_out);
  and and_3 (and_3_out, q1, 1'b1);
  or or_2 (or_2_out, and_3_out, and_5_out);
  // D_Flip_Flop d_flip_flop_1: pin names not known; wires that end beside it: or_1_out, quotient_clk_out, q1
  and and_4 (and_4_out, q2, 1'b1);
  and and_5 (and_5_out, not_1_out, 1'b0);
  // D_Flip_Flop d_flip_flop_2: pin names not known; wires that end beside it: or_2_out, quotient_clk_out, q2
  and and_6 (and_6_out, not_1_out, 1'b0);
  or or_3 (or_3_out, and_4_out, and_6_out);
  // D_Flip_Flop d_flip_flop_3: pin names not known; wires that end beside it: or_3_out, quotient_clk_out, q3
  and and_7 (and_7_out, q3, 1'b1);
  and and_8 (and_8_out, not_1_out, 1'b0);
  or or_4 (or_4_out, and_7_out, and_8_out);
  and and_9 (and_9_out, q4, 1'b1);
  or or_5 (or_5_out, and_9_out, and_10_out);
  // D_Flip_Flop d_flip_flop_4: pin names not known; wires that end beside it: or_4_out, quotient_clk_out, q4
  and and_10 (and_10_out, not_1_out, 1'b0);
  // D_Flip_Flop d_flip_flop_5: pin names not known; wires that end beside it: or_5_out, quotient_clk_out, q5
  and and_11 (and_11_out, not_1_out, 1'b0);
  and and_12 (and_12_out, q5, 1'b1);
  or or_6 (or_6_out, and_12_out, and_11_out);
  and and_13 (and_13_out, q6, 1'b1);
  // D_Flip_Flop d_flip_flop_6: pin names not known; wires that end beside it: or_6_out, quotient_clk_out
  and and_14 (and_14_out, not_1_out, 1'b0);
  or or_7 (or_7_out, and_13_out, and_14_out);
  and and_15 (and_15_out, q7, 1'b1);
  or or_8 (or_8_out, and_15_out, and_16_out);
  // D_Flip_Flop d_flip_flop_7: pin names not known; wires that end beside it: or_7_out, quotient_clk_out, q7
  and and_16 (and_16_out, not_1_out, 1'b0);
  and and_17 (and_17_out, q8, 1'b1);
  // D_Flip_Flop d_flip_flop_8: pin names not known; wires that end beside it: or_8_out, quotient_clk_out, q8, q8
  and and_18 (and_18_out, not_1_out, 1'b0);
  or or_9 (or_9_out, and_17_out, and_18_out);
  // D_Flip_Flop d_flip_flop_9: pin names not known; wires that end beside it: or_9_out, quotient_clk_out, q9
endmodule
